// Logisim project hw4.circ as structural Verilog: 10 circuits, main circuit main
module main (
  input  reset
);

  wire add, addi, ALU_branch_eq, ALU_branch_gt, alu_mux, and_1_out, and_2_out, ands, beq, bgt, clk, dwe,
       file_mux, in, in_1, j, jr, m_latch_oe_latched, m_latch_we_latched, not_1_out, ors, out, rd_1, rwe,
       shl, shra, sub;
  wire [1:0] pc_mux;
  wire [2:0] aluop, multiplexer_1_out, multiplexer_4_out;
  wire [3:0] rom_1_data_2;
  wire [6:0] keyboard_1_data, reg_file_rs_contents_2;
  wire [11:0] rom_1_data;
  wire [15:0] adder_16bit_1_result, adder_16bit_2_result, ALU_data_out, bit_extender_1_out,
       m_latch_address_latched, m_latch_data_in_latched, multiplexer_2_out, multiplexer_3_out,
       multiplexer_5_out, multiplexer_6_out, multiplexer_7_out, multiplexer_8_out, multiplexer_9_out,
       PC_data_out, ram_1_dout, reg_file_rt_contents;
  wire [15:7] reg_file_rs_contents, undriven;

  Clock clock_1 (.out(clk));
  \reg  PC (.data_in(multiplexer_8_out), .clk(clk), .write_enable(1'b1), .reset(reset), .data_out(PC_data_out));
  ROM #(.addrWidth(16), .dataWidth(16)) rom_1 (.addr(PC_data_out), .data({rom_1_data_2, rom_1_data}));
  adder_16bit adder_16bit_1 (.A(PC_data_out), .B(16'h1), .result(adder_16bit_1_result));  // open: ovf
  Decoder #(.select(4)) decoder_1 (
    .out0(out), .out1(in), .out2(file_mux), .out3(dwe), .out4(beq), .out5(bgt), .out6(ors), .out7(ands),
    .out8(addi), .out9(add), .out10(sub), .out11(shra), .out12(shl), .out13(j), .out14(in_1), .out15(jr),
    .sel(rom_1_data_2), .en(1'b1));
  Multiplexer #(.width(3), .enable("false")) multiplexer_1 (
    .in0(rom_1_data[5:3]), .in1(rom_1_data[8:6]), .out(multiplexer_1_out), .sel(rd_1));
  not not_1 (not_1_out, clk);
  Multiplexer #(.width(16), .enable("false")) multiplexer_2 (
    .in0(multiplexer_9_out), .in1(adder_16bit_1_result), .out(multiplexer_2_out), .sel(in_1));
  Multiplexer #(.width(16), .enable("false")) multiplexer_3 (
    .in0(multiplexer_2_out), .in1({undriven, keyboard_1_data}), .out(multiplexer_3_out), .sel(in));
  Multiplexer #(.width(3), .enable("false")) multiplexer_4 (
    .in0(multiplexer_1_out), .in1(3'b111), .out(multiplexer_4_out), .sel(in_1));
  RegisterFile reg_file (
    .rd(multiplexer_4_out), .data_in(multiplexer_3_out), .clk(not_1_out), .write_enable(rwe), .reset(reset),
    .rs(rom_1_data[11:9]), .rt(rom_1_data[8:6]),
    .rs_contents({reg_file_rs_contents, reg_file_rs_contents_2}), .rt_contents(reg_file_rt_contents));
  or or_1 (rd_1, addi, file_mux);
  assign bit_extender_1_out = {{10{rom_1_data[5]}}, rom_1_data[5:0]};  // Bit_Extender bit_extender_1
  or or_2 (alu_mux, addi, dwe, file_mux);
  Multiplexer #(.width(16), .enable("false")) multiplexer_5 (
    .in0(reg_file_rt_contents), .in1(bit_extender_1_out), .out(multiplexer_5_out), .sel(alu_mux));
  Keyboard #(.trigger("falling")) keyboard_1 (.clk(clk), .re(in), .clr(reset), .data(keyboard_1_data));  // open: avail
  adder_16bit adder_16bit_2 (
    .A(adder_16bit_1_result), .B(bit_extender_1_out), .result(adder_16bit_2_result));  // open: ovf
  Alu_comp ALU (
    .rs({reg_file_rs_contents, reg_file_rs_contents_2}), .rt(multiplexer_5_out), .shift(rom_1_data[2:0]),
    .opcode(aluop), .branch_eq(ALU_branch_eq), .branch_gt(ALU_branch_gt), .data_out(ALU_data_out));
  or or_3 (pc_mux[1], beq, bgt, jr);
  and and_1 (and_1_out, beq, ALU_branch_eq);
  memory_latch m_latch (
    .address(ALU_data_out), .WE(dwe), .clk(clk), .data_in(reg_file_rt_contents),
    .address_latched(m_latch_address_latched), .WE_latched(m_latch_we_latched),
    .OE_latched(m_latch_oe_latched), .data_in_latched(m_latch_data_in_latched));
  or or_4 (pc_mux[0], in_1, j, jr);
  TTY #(.rows(13), .cols(80), .trigger("falling")) tty_1 (
    .data(reg_file_rs_contents_2), .clk(clk), .we(out), .clr(reset));
  Multiplexer #(.width(16), .enable("false")) multiplexer_6 (
    .in0(adder_16bit_1_result), .in1(adder_16bit_2_result), .out(multiplexer_6_out), .sel(and_1_out));
  and and_2 (and_2_out, bgt, ALU_branch_gt);
  RAM #(.addrWidth(16), .dataWidth(16), .trigger("high"), .databus("bibus")) ram_1 (
    .addr(m_latch_address_latched), .we(m_latch_we_latched), .oe(m_latch_oe_latched),
    .din(m_latch_data_in_latched), .dout(ram_1_dout));
  or or_5 (rwe, in, file_mux, ors, ands, addi, add, sub, shra, shl, in_1);
  Multiplexer #(.width(16), .enable("false")) multiplexer_7 (
    .in0(multiplexer_6_out), .in1(adder_16bit_2_result), .out(multiplexer_7_out), .sel(and_2_out));
  Multiplexer #(.select(2), .width(16), .enable("false")) multiplexer_8 (
    .in0(adder_16bit_1_result), .in1({PC_data_out[15:12], rom_1_data}), .in2(multiplexer_7_out),
    .in3({reg_file_rs_contents, reg_file_rs_contents_2}), .out(multiplexer_8_out), .sel(pc_mux));
  or or_6 (aluop[2], dwe, shra, shl, addi, add, file_mux);
  Multiplexer #(.width(16), .enable("false")) multiplexer_9 (
    .in0(ALU_data_out), .in1(ram_1_dout), .out(multiplexer_9_out), .sel(file_mux));
  or or_7 (aluop[1], dwe, ands, ors, addi, add, file_mux);
  or or_8 (aluop[0], sub, ors, shl);

  // Other names for the same wires on the sheet: in_2 = in; lw = file_mux; jal = in_1; rd_2 = in_1; rst = reset;
  //   sw = dwe

  // Notes on the sheet:
  //   contents of rom_1 (hex, n*v repeats v):
  //   80c0 804f 8090 5441 403f e009 4206 d00f 9488 8272 fe00 8441 403f 8441 403f 403f
endmodule

module \reg  (
  input  [15:0] data_in,
  input  clk,
  input  write_enable,
  input  reset,
  output [15:0] data_out
);

  wire and_1_out;

  and and_1 (and_1_out, clk, write_enable);
  D_Flip_Flop d_ff_1 (.D(data_in[0]), .clk(and_1_out), .Q(data_out[0]), .reset(reset));  // open: Qn, preset
  D_Flip_Flop d_ff_2 (.D(data_in[1]), .clk(and_1_out), .Q(data_out[1]), .reset(reset));  // open: Qn, preset
  D_Flip_Flop d_ff_3 (.D(data_in[2]), .clk(and_1_out), .Q(data_out[2]), .reset(reset));  // open: Qn, preset
  D_Flip_Flop d_ff_4 (.D(data_in[3]), .clk(and_1_out), .Q(data_out[3]), .reset(reset));  // open: Qn, preset
  D_Flip_Flop d_ff_5 (.D(data_in[4]), .clk(and_1_out), .Q(data_out[4]), .reset(reset));  // open: Qn, preset
  D_Flip_Flop d_ff_6 (.D(data_in[5]), .clk(and_1_out), .Q(data_out[5]), .reset(reset));  // open: Qn, preset
  D_Flip_Flop d_ff_7 (.D(data_in[6]), .clk(and_1_out), .Q(data_out[6]), .reset(reset));  // open: Qn, preset
  D_Flip_Flop d_ff_8 (.D(data_in[7]), .clk(and_1_out), .Q(data_out[7]), .reset(reset));  // open: Qn, preset
  D_Flip_Flop d_ff_9 (.D(data_in[8]), .clk(and_1_out), .Q(data_out[8]), .reset(reset));  // open: Qn, preset
  D_Flip_Flop d_ff_10 (.D(data_in[9]), .clk(and_1_out), .Q(data_out[9]), .reset(reset));  // open: Qn, preset
  D_Flip_Flop d_ff_11 (.D(data_in[10]), .clk(and_1_out), .Q(data_out[10]), .reset(reset));  // open: Qn, preset
  D_Flip_Flop d_ff_12 (.D(data_in[11]), .clk(and_1_out), .Q(data_out[11]), .reset(reset));  // open: Qn, preset
  D_Flip_Flop d_ff_13 (.D(data_in[12]), .clk(and_1_out), .Q(data_out[12]), .reset(reset));  // open: Qn, preset
  D_Flip_Flop d_ff_14 (.D(data_in[13]), .clk(and_1_out), .Q(data_out[13]), .reset(reset));  // open: Qn, preset
  D_Flip_Flop d_ff_15 (.D(data_in[14]), .clk(and_1_out), .Q(data_out[14]), .reset(reset));  // open: Qn, preset
  D_Flip_Flop d_ff_16 (.D(data_in[15]), .clk(and_1_out), .Q(data_out[15]), .reset(reset));  // open: Qn, preset
endmodule

module RegisterFile (
  input  [2:0] rd,
  input  [15:0] data_in,
  input  clk,
  input  write_enable,
  input  reset,
  input  [2:0] rs,
  input  [2:0] rt,
  output [15:0] rs_contents,
  output [15:0] rt_contents
);

  wire decoder_1_out1, decoder_1_out2, decoder_1_out3, decoder_1_out4, decoder_1_out5, decoder_1_out6,
       decoder_1_out7;
  wire [15:0] reg_1_data_out, reg_2_data_out, reg_3_data_out, reg_4_data_out, reg_5_data_out, reg_6_data_out,
       reg_7_data_out;

  Decoder #(.select(3)) decoder_1 (
    .out1(decoder_1_out1), .out2(decoder_1_out2), .out3(decoder_1_out3), .out4(decoder_1_out4),
    .out5(decoder_1_out5), .out6(decoder_1_out6), .out7(decoder_1_out7), .sel(rd), .en(write_enable));  // open: out0
  // Probe on {16{1'b0}}
  \reg  reg_1 (.data_in(data_in), .clk(clk), .write_enable(decoder_1_out1), .reset(reset), .data_out(reg_1_data_out));
  \reg  reg_2 (.data_in(data_in), .clk(clk), .write_enable(decoder_1_out2), .reset(reset), .data_out(reg_2_data_out));
  \reg  reg_3 (.data_in(data_in), .clk(clk), .write_enable(decoder_1_out3), .reset(reset), .data_out(reg_3_data_out));
  \reg  reg_4 (.data_in(data_in), .clk(clk), .write_enable(decoder_1_out4), .reset(reset), .data_out(reg_4_data_out));
  \reg  reg_5 (.data_in(data_in), .clk(clk), .write_enable(decoder_1_out5), .reset(reset), .data_out(reg_5_data_out));
  \reg  reg_6 (.data_in(data_in), .clk(clk), .write_enable(decoder_1_out6), .reset(reset), .data_out(reg_6_data_out));
  \reg  reg_7 (.data_in(data_in), .clk(clk), .write_enable(decoder_1_out7), .reset(reset), .data_out(reg_7_data_out));
  // Probe on reg_1_data_out
  // Probe on reg_2_data_out
  // Probe on reg_3_data_out
  // Probe on reg_4_data_out
  // Probe on reg_5_data_out
  // Probe on reg_6_data_out
  // Probe on reg_7_data_out
  Multiplexer #(.select(3), .width(16), .enable("false")) multiplexer_1 (
    .in0({16{1'b0}}), .in1(reg_1_data_out), .in2(reg_2_data_out), .in3(reg_3_data_out), .in4(reg_4_data_out),
    .in5(reg_5_data_out), .in6(reg_6_data_out), .in7(reg_7_data_out), .out(rs_contents), .sel(rs));
  Multiplexer #(.select(3), .width(16), .enable("false")) multiplexer_2 (
    .in0({16{1'b0}}), .in1(reg_1_data_out), .in2(reg_2_data_out), .in3(reg_3_data_out), .in4(reg_4_data_out),
    .in5(reg_5_data_out), .in6(reg_6_data_out), .in7(reg_7_data_out), .out(rt_contents), .sel(rt));
endmodule

module adder (
  input  c_in,
  input  inA,
  input  inB,
  output sum,
  output c_out
);

  wire and_1_out, and_2_out, xor_1_out;

  and and_1 (and_1_out, inB, inA);
  or or_1 (c_out, and_1_out, and_2_out);
  xor xor_1 (xor_1_out, inA, inB);
  and and_2 (and_2_out, xor_1_out, c_in);
  xor xor_2 (sum, c_in, xor_1_out);
endmodule

// addr
module adder_16bit (
  input  [15:0] A,
  input  [15:0] B,
  output ovf,
  output [15:0] result
);

  wire adder_1_c_out, adder_2_c_out, adder_3_c_out, adder_4_c_out, adder_5_c_out, adder_6_c_out,
       adder_7_c_out, adder_8_c_out, adder_9_c_out, adder_10_c_out, adder_11_c_out, adder_12_c_out,
       adder_13_c_out, adder_14_c_out, adder_15_c_out, adder_16_c_out, xor_2_out, xor_3_out, xor_4_out,
       xor_5_out, xor_6_out, xor_7_out, xor_8_out, xor_9_out, xor_10_out, xor_11_out, xor_12_out, xor_13_out,
       xor_14_out, xor_15_out, xor_16_out, xor_17_out;

  xor xor_1 (ovf, adder_1_c_out, adder_2_c_out);
  adder adder_1 (.inA(A[15]), .inB(xor_2_out), .sum(result[15]), .c_in(adder_2_c_out), .c_out(adder_1_c_out));
  xor xor_2 (xor_2_out, 1'b0, B[15]);
  xor xor_3 (xor_3_out, 1'b0, B[14]);
  adder adder_2 (.inA(A[14]), .inB(xor_3_out), .sum(result[14]), .c_in(adder_3_c_out), .c_out(adder_2_c_out));
  adder adder_3 (.inA(A[13]), .inB(xor_4_out), .sum(result[13]), .c_in(adder_4_c_out), .c_out(adder_3_c_out));
  xor xor_4 (xor_4_out, 1'b0, B[13]);
  xor xor_5 (xor_5_out, 1'b0, B[12]);
  adder adder_4 (.inA(A[12]), .inB(xor_5_out), .sum(result[12]), .c_in(adder_5_c_out), .c_out(adder_4_c_out));
  adder adder_5 (.inA(A[11]), .inB(xor_6_out), .sum(result[11]), .c_in(adder_6_c_out), .c_out(adder_5_c_out));
  xor xor_6 (xor_6_out, 1'b0, B[11]);
  xor xor_7 (xor_7_out, 1'b0, B[10]);
  adder adder_6 (.inA(A[10]), .inB(xor_7_out), .sum(result[10]), .c_in(adder_7_c_out), .c_out(adder_6_c_out));
  adder adder_7 (.inA(A[9]), .inB(xor_8_out), .sum(result[9]), .c_in(adder_8_c_out), .c_out(adder_7_c_out));
  xor xor_8 (xor_8_out, 1'b0, B[9]);
  xor xor_9 (xor_9_out, 1'b0, B[8]);
  adder adder_8 (.inA(A[8]), .inB(xor_9_out), .sum(result[8]), .c_in(adder_9_c_out), .c_out(adder_8_c_out));
  adder adder_9 (.inA(A[7]), .inB(xor_10_out), .sum(result[7]), .c_in(adder_10_c_out), .c_out(adder_9_c_out));
  xor xor_10 (xor_10_out, 1'b0, B[7]);
  xor xor_11 (xor_11_out, 1'b0, B[6]);
  adder adder_10 (.inA(A[6]), .inB(xor_11_out), .sum(result[6]), .c_in(adder_11_c_out), .c_out(adder_10_c_out));
  adder adder_11 (.inA(A[5]), .inB(xor_12_out), .sum(result[5]), .c_in(adder_12_c_out), .c_out(adder_11_c_out));
  xor xor_12 (xor_12_out, 1'b0, B[5]);
  xor xor_13 (xor_13_out, 1'b0, B[4]);
  adder adder_12 (.inA(A[4]), .inB(xor_13_out), .sum(result[4]), .c_in(adder_13_c_out), .c_out(adder_12_c_out));
  adder adder_13 (.inA(A[3]), .inB(xor_14_out), .sum(result[3]), .c_in(adder_14_c_out), .c_out(adder_13_c_out));
  xor xor_14 (xor_14_out, 1'b0, B[3]);
  xor xor_15 (xor_15_out, 1'b0, B[2]);
  adder adder_14 (.inA(A[2]), .inB(xor_15_out), .sum(result[2]), .c_in(adder_15_c_out), .c_out(adder_14_c_out));
  adder adder_15 (.inA(A[1]), .inB(xor_16_out), .sum(result[1]), .c_in(adder_16_c_out), .c_out(adder_15_c_out));
  xor xor_16 (xor_16_out, 1'b0, B[1]);
  xor xor_17 (xor_17_out, 1'b0, B[0]);
  adder adder_16 (.inA(A[0]), .inB(xor_17_out), .sum(result[0]), .c_in(1'b0), .c_out(adder_16_c_out));
endmodule

// sub
module sub_16bit (
  input  [15:0] A,
  input  [15:0] B,
  output ovf,
  output [15:0] result
);

  wire adder_1_c_out, adder_2_c_out, adder_3_c_out, adder_4_c_out, adder_5_c_out, adder_6_c_out,
       adder_7_c_out, adder_8_c_out, adder_9_c_out, adder_10_c_out, adder_11_c_out, adder_12_c_out,
       adder_13_c_out, adder_14_c_out, adder_15_c_out, adder_16_c_out, xor_2_out, xor_3_out, xor_4_out,
       xor_5_out, xor_6_out, xor_7_out, xor_8_out, xor_9_out, xor_10_out, xor_11_out, xor_12_out, xor_13_out,
       xor_14_out, xor_15_out, xor_16_out, xor_17_out;

  xor xor_1 (ovf, adder_1_c_out, adder_2_c_out);
  adder adder_1 (.inA(A[15]), .inB(xor_2_out), .sum(result[15]), .c_in(adder_2_c_out), .c_out(adder_1_c_out));
  xor xor_2 (xor_2_out, 1'b1, B[15]);
  xor xor_3 (xor_3_out, 1'b1, B[14]);
  adder adder_2 (.inA(A[14]), .inB(xor_3_out), .sum(result[14]), .c_in(adder_3_c_out), .c_out(adder_2_c_out));
  adder adder_3 (.inA(A[13]), .inB(xor_4_out), .sum(result[13]), .c_in(adder_4_c_out), .c_out(adder_3_c_out));
  xor xor_4 (xor_4_out, 1'b1, B[13]);
  xor xor_5 (xor_5_out, 1'b1, B[12]);
  adder adder_4 (.inA(A[12]), .inB(xor_5_out), .sum(result[12]), .c_in(adder_5_c_out), .c_out(adder_4_c_out));
  adder adder_5 (.inA(A[11]), .inB(xor_6_out), .sum(result[11]), .c_in(adder_6_c_out), .c_out(adder_5_c_out));
  xor xor_6 (xor_6_out, 1'b1, B[11]);
  xor xor_7 (xor_7_out, 1'b1, B[10]);
  adder adder_6 (.inA(A[10]), .inB(xor_7_out), .sum(result[10]), .c_in(adder_7_c_out), .c_out(adder_6_c_out));
  adder adder_7 (.inA(A[9]), .inB(xor_8_out), .sum(result[9]), .c_in(adder_8_c_out), .c_out(adder_7_c_out));
  xor xor_8 (xor_8_out, 1'b1, B[9]);
  xor xor_9 (xor_9_out, 1'b1, B[8]);
  adder adder_8 (.inA(A[8]), .inB(xor_9_out), .sum(result[8]), .c_in(adder_9_c_out), .c_out(adder_8_c_out));
  adder adder_9 (.inA(A[7]), .inB(xor_10_out), .sum(result[7]), .c_in(adder_10_c_out), .c_out(adder_9_c_out));
  xor xor_10 (xor_10_out, 1'b1, B[7]);
  xor xor_11 (xor_11_out, 1'b1, B[6]);
  adder adder_10 (.inA(A[6]), .inB(xor_11_out), .sum(result[6]), .c_in(adder_11_c_out), .c_out(adder_10_c_out));
  adder adder_11 (.inA(A[5]), .inB(xor_12_out), .sum(result[5]), .c_in(adder_12_c_out), .c_out(adder_11_c_out));
  xor xor_12 (xor_12_out, 1'b1, B[5]);
  xor xor_13 (xor_13_out, 1'b1, B[4]);
  adder adder_12 (.inA(A[4]), .inB(xor_13_out), .sum(result[4]), .c_in(adder_13_c_out), .c_out(adder_12_c_out));
  adder adder_13 (.inA(A[3]), .inB(xor_14_out), .sum(result[3]), .c_in(adder_14_c_out), .c_out(adder_13_c_out));
  xor xor_14 (xor_14_out, 1'b1, B[3]);
  xor xor_15 (xor_15_out, 1'b1, B[2]);
  adder adder_14 (.inA(A[2]), .inB(xor_15_out), .sum(result[2]), .c_in(adder_15_c_out), .c_out(adder_14_c_out));
  adder adder_15 (.inA(A[1]), .inB(xor_16_out), .sum(result[1]), .c_in(adder_16_c_out), .c_out(adder_15_c_out));
  xor xor_16 (xor_16_out, 1'b1, B[1]);
  xor xor_17 (xor_17_out, 1'b1, B[0]);
  adder adder_16 (.inA(A[0]), .inB(xor_17_out), .sum(result[0]), .c_in(1'b1), .c_out(adder_16_c_out));
endmodule

module Alu_comp (
  input  [15:0] rs,
  input  [15:0] rt,
  input  [2:0] shift,
  input  [2:0] opcode,
  output branch_eq,
  output branch_gt,
  output [15:0] data_out
);

  wire not_1_out, not_2_out, not_3_out, not_4_out, not_5_out, not_6_out, not_7_out, not_8_out, not_9_out,
       not_10_out, not_11_out, not_12_out, not_13_out, not_14_out, not_15_out, not_16_out;
  wire [14:0] sub_16bit_1_result;
  wire [15:0] a_shifter_1_data_out, adder_16bit_1_result, and_1_out, l_shifter_1_data_out, or_1_out,
       sub_16bit_2_result;

  sub_16bit sub_16bit_1 (.A(rt), .B(rs), .result({branch_gt, sub_16bit_1_result}));  // open: ovf
  not not_1 (not_1_out, sub_16bit_1_result[0]);
  not not_2 (not_2_out, sub_16bit_1_result[1]);
  not not_3 (not_3_out, sub_16bit_1_result[2]);
  not not_4 (not_4_out, sub_16bit_1_result[3]);
  not not_5 (not_5_out, sub_16bit_1_result[4]);
  not not_6 (not_6_out, sub_16bit_1_result[5]);
  not not_7 (not_7_out, sub_16bit_1_result[6]);
  not not_8 (not_8_out, sub_16bit_1_result[7]);
  not not_9 (not_9_out, sub_16bit_1_result[8]);
  not not_10 (not_10_out, sub_16bit_1_result[9]);
  not not_11 (not_11_out, sub_16bit_1_result[10]);
  not not_12 (not_12_out, sub_16bit_1_result[11]);
  not not_13 (not_13_out, sub_16bit_1_result[12]);
  not not_14 (not_14_out, sub_16bit_1_result[13]);
  not not_15 (not_15_out, sub_16bit_1_result[14]);
  not not_16 (not_16_out, branch_gt);
  adder_16bit adder_16bit_1 (.A(rs), .B(rt), .result(adder_16bit_1_result));  // open: ovf
  sub_16bit sub_16bit_2 (.A(rs), .B(rt), .result(sub_16bit_2_result));  // open: ovf
  assign and_1_out = rs & rt;  // AND_Gate and_1, 16 bits wide
  assign or_1_out = rs | rt;  // OR_Gate or_1, 16 bits wide
  a_shifter a_shifter_1 (.data_in(rs), .shift(shift), .data_out(a_shifter_1_data_out));
  l_shifter l_shifter_1 (.data_in(rs), .shift(shift), .data_out(l_shifter_1_data_out));
  and and_2 (branch_eq, not_1_out, not_2_out, not_3_out, not_4_out, not_5_out, not_6_out, not_7_out, not_8_out, not_9_out, not_10_out, not_11_out, not_12_out, not_13_out, not_14_out, not_15_out, not_16_out);
  Multiplexer #(.select(3), .width(16), .enable("false")) multiplexer_1 (
    .in0({16{1'b0}}), .in1(sub_16bit_2_result), .in2(and_1_out), .in3(or_1_out), .in4(a_shifter_1_data_out),
    .in5(l_shifter_1_data_out), .in6(adder_16bit_1_result), .out(data_out), .sel(opcode));  // open: in7
endmodule

// arith
module a_shifter (
  input  [15:0] data_in,
  input  [2:0] shift,
  output [15:0] data_out
);

  Multiplexer #(.select(3), .width(16), .enable("false")) multiplexer_1 (
    .in0(data_in), .in1({{2{data_in[15]}}, data_in[14:1]}), .in2({{3{data_in[15]}}, data_in[14:2]}),
    .in3({{4{data_in[15]}}, data_in[14:3]}), .in4({{5{data_in[15]}}, data_in[14:4]}),
    .in5({{6{data_in[15]}}, data_in[14:5]}), .in6({{7{data_in[15]}}, data_in[14:6]}),
    .in7({{8{data_in[15]}}, data_in[14:7]}), .out(data_out), .sel(shift));
endmodule

// logic
module l_shifter (
  input  [15:0] data_in,
  input  [2:0] shift,
  output [15:0] data_out
);

  Multiplexer #(.select(3), .width(16), .enable("false")) multiplexer_1 (
    .in0(data_in), .in1({data_in[14:0], 1'b0}), .in2({data_in[13:0], 2'b00}), .in3({data_in[12:0], 3'b000}),
    .in4({data_in[11:0], 4'b0000}), .in5({data_in[10:0], {5{1'b0}}}), .in6({data_in[9:0], {6{1'b0}}}),
    .in7({data_in[8:0], {7{1'b0}}}), .out(data_out), .sel(shift));
endmodule

module memory_latch (
  input  [15:0] address,
  input  WE,
  input  clk,
  input  [15:0] data_in,
  output [15:0] address_latched,
  output WE_latched,
  output OE_latched,
  output [15:0] data_in_latched
);

  wire d_ff_1_q;
  wire [15:0] register_1_q;

  Register #(.width(16), .trigger("falling")) register_1 (
    .D(address), .en(WE), .clk(clk), .Q(register_1_q));  // open: clr
  Register #(.width(16), .trigger("falling")) register_2 (
    .D(data_in), .en(WE), .clk(clk), .Q(data_in_latched));  // open: clr
  D_Flip_Flop #(.trigger("falling")) d_ff_1 (.D(WE), .clk(clk), .Q(d_ff_1_q));  // open: Qn, preset, reset
  Multiplexer #(.width(16), .enable("false")) multiplexer_1 (
    .in0(address), .in1(register_1_q), .out(address_latched), .sel(d_ff_1_q));
  and and_1 (WE_latched, clk, d_ff_1_q);
  not not_1 (OE_latched, WE_latched);
endmodule
